// Logisim project s-mips.circ as structural Verilog
module S_MIPS_Board (
  input  DESHABILITAR_DISPATCHER,
  output halt
);

  wire button_1_out, CLK, CS, d_ff_1_q, LCLR, LoadRAM, LoadRAMOn, LW, R_R_W, R_W, ram_dispatcher_1_finished,
       RCS, Reset_out, RST, TTY_EN;
  wire [2:0] KDB;
  wire [3:0] LMask, Mask, ram_1_read_time, ram_1_write_time, RMask;
  wire [6:0] KDB_DATA, TTY_DATA;
  wire [15:0] Addr, LAddr, RAddr;
  wire [31:0] I0, I1, I2, I3, LData, ram_1_data_out_0, ram_1_data_out_1, ram_1_data_out_2, ram_1_data_out_3,
       RI0, RI1, RI2, RI3;

  TTY #(.rows(25), .cols(80)) tty_1 (.data(TTY_DATA), .clk(CLK), .we(TTY_EN), .clr(RST));
  not not_1 (LoadRAMOn, ram_dispatcher_1_finished);
  RAM_Dispatcher ram_dispatcher_1 (
    .WriteTime(ram_1_write_time), .Clock(CLK), .Data(LData), .Address(LAddr), .Mask(LMask),
    .Finished(ram_dispatcher_1_finished), .Write(LW), .CLR(LCLR));
  Keyboard #(.buflen(64)) keyboard_1 (.clk(CLK), .re(KDB[0]), .avail(KDB[2]), .data(KDB_DATA));  // open: clr
  RAM ram_1 (
    .Data_Out_0(ram_1_data_out_0), .Data_Out_1(ram_1_data_out_1), .Data_Out_2(ram_1_data_out_2),
    .Data_Out_3(ram_1_data_out_3), .Data_In_0(RI0), .Data_In_1(RI1), .Data_In_2(RI2), .Data_In_3(RI3),
    .Mask(RMask), .nRead_Write(R_R_W), .Chip_Select(RCS), .Read_Time(ram_1_read_time), .Reset(button_1_out),
    .Write_Time(ram_1_write_time), .in_1(RAddr));
  Button button_1 (.out(button_1_out));
  D_Flip_Flop d_ff_1 (.clk(CLK), .D(1'b1), .Q(d_ff_1_q), .reset(Reset_out));  // open: Qn, preset, en
  Button Reset (.out(Reset_out));
  S_MIPS s_mips_1 (
    .Kbd_Enable(KDB[0]), .Address(Addr), .Kbd_Clear(KDB[1]), .Kbd_Available(KDB[2]), .RAM_In_0(I0),
    .Kbd_ASCII_Data(KDB_DATA), .RAM_In_1(I1), .TTY_Enable(TTY_EN), .RAM_In_2(I2), .RAM_In_3(I3),
    .TTY_ASCII_Data(TTY_DATA), .Stop(halt), .Mask(Mask), .Read_Time(ram_1_read_time),
    .Write_Time(ram_1_write_time), .nRead_Write(R_W), .Chip_Select(CS), .Clock(CLK), .Reset(RST),
    .RAM_Out_0(ram_1_data_out_0), .RAM_Out_1(ram_1_data_out_1), .RAM_Out_2(ram_1_data_out_2),
    .RAM_Out_3(ram_1_data_out_3));
  D_Flip_Flop d_ff_2 (.clk(CLK), .D(d_ff_1_q), .Qn(LCLR), .reset(Reset_out));  // open: Q, preset, en
  or or_1 (RST, LCLR, LoadRAM);
  Clock clock_1 (.out(CLK));
  Multiplexer #(.width(32), .enable("false")) multiplexer_1 (.in0(I0), .in1(LData), .out(RI0), .sel(LoadRAM));
  Multiplexer #(.width(32), .enable("false")) multiplexer_2 (.in0(I1), .in1(LData), .out(RI1), .sel(LoadRAM));
  Multiplexer #(.width(32), .enable("false")) multiplexer_3 (.in0(I2), .in1(LData), .out(RI2), .sel(LoadRAM));
  Multiplexer #(.width(32), .enable("false")) multiplexer_4 (.in0(I3), .in1(LData), .out(RI3), .sel(LoadRAM));
  and and_1 (LoadRAM, ~DESHABILITAR_DISPATCHER, LoadRAMOn);  // AND_Gate
  Multiplexer #(.width(16), .enable("false")) multiplexer_5 (.in0(Addr), .in1(LAddr), .out(RAddr), .sel(LoadRAM));
  Multiplexer #(.width(4), .enable("false")) multiplexer_6 (.in0(Mask), .in1(LMask), .out(RMask), .sel(LoadRAM));
  Multiplexer #(.enable("false")) multiplexer_7 (.in0(CS), .in1(LW), .out(RCS), .sel(LoadRAM));
  Multiplexer #(.enable("false")) multiplexer_8 (.in0(R_W), .in1(LW), .out(R_R_W), .sel(LoadRAM));

  // Notes on the sheet:
  //   NO MODIFICAR
  //   Keyboard
endmodule

module RAM (
  input  [15:0] in_1,
  input  [31:0] Data_In_0,
  input  [31:0] Data_In_1,
  input  [31:0] Data_In_2,
  input  [31:0] Data_In_3,
  input  [3:0] Mask,
  input  nRead_Write,
  input  Chip_Select,
  input  Reset,
  output [31:0] Data_Out_0,
  output [31:0] Data_Out_1,
  output [31:0] Data_Out_2,
  output [31:0] Data_Out_3,
  output [3:0] Read_Time,
  output [3:0] Write_Time
);

  wire and_2_out, and_3_out, and_4_out, and_5_out, and_6_out, and_7_out, and_8_out, and_9_out, Changed, CLK,
       comparator_2_eq, comparator_3_eq, comparator_4_eq, comparator_5_eq, comparator_6_eq, Count,
       demultiplexer_3_out0, Idle, Idle_q, Load, Load0, Load1, nand_1_out, or_1_out, or_2_out, or_3_out,
       or_4_out, or_5_out, or_6_out, or_7_out, or_8_out, or_9_out, or_10_out, Proc_q, Update_Mem, Zero_Time;
  wire [3:0] counter_1_q, multiplexer_1_out, subtractor_1_out;
  wire [31:0] register_1_q, register_2_q, register_3_q, register_4_q, register_5_q;

  // Probe on 4'b0011
  // Probe on 4'b0010
  Multiplexer #(.width(4), .enable("false")) multiplexer_1 (
    .in0(4'b0011), .in1(4'b0010), .out(multiplexer_1_out), .sel(nRead_Write));
  or or_1 (or_1_out, Idle, Update_Mem);
  or or_2 (or_2_out, ~Chip_Select, Reset);  // OR_Gate
  Subtractor #(.width(4)) subtractor_1 (.a(multiplexer_1_out), .b(4'b0010), .out(subtractor_1_out));  // open: bin, bout
  Demultiplexer #(.enable("false")) demultiplexer_1 (.out0(Idle), .out1(Load0), .in(Idle_q), .sel(Changed));
  D_Flip_Flop u_Idle (.clk(CLK), .D(or_1_out), .Q(Idle_q), .preset(or_2_out));  // open: Qn, en, reset
  // Probe on counter_1_q
  Counter #(.width(4), .max('hf)) counter_1 (
    .load(Load), .D(subtractor_1_out), .count(Count), .Q(counter_1_q), .clk(CLK), .clr(or_3_out));  // open: carry
  or or_3 (or_3_out, ~Chip_Select, Reset);  // OR_Gate
  Comparator #(.width(4), .mode("unsigned")) comparator_1 (
    .a(4'b0000), .b(counter_1_q), .eq(Zero_Time));  // open: gt, lt
  or or_4 (or_4_out, Count, Load0, Load1);
  Register #(.width(32)) register_1 (.D(Data_In_0), .en(Chip_Select), .Q(register_1_q), .clk(CLK), .clr(or_5_out));
  or or_5 (or_5_out, ~Chip_Select, Reset);  // OR_Gate
  Register #(.width(32)) register_2 (.D(Data_In_1), .en(Chip_Select), .Q(register_2_q), .clk(CLK), .clr(or_6_out));
  or or_6 (or_6_out, ~Chip_Select, Reset);  // OR_Gate
  Register #(.width(32)) register_3 (.D(Data_In_2), .en(Chip_Select), .Q(register_3_q), .clk(CLK), .clr(or_7_out));
  or or_7 (or_7_out, ~Chip_Select, Reset);  // OR_Gate
  Register #(.width(32)) register_4 (.D(Data_In_3), .en(Chip_Select), .Q(register_4_q), .clk(CLK), .clr(or_8_out));
  or or_8 (or_8_out, ~Chip_Select, Reset);  // OR_Gate
  Register #(.width(32)) register_5 (
    .D({{11{1'b1}}, nRead_Write, Mask, in_1}), .en(Chip_Select), .Q(register_5_q), .clk(CLK), .clr(or_9_out));
  or or_9 (or_9_out, ~Chip_Select, Reset);  // OR_Gate
  D_Flip_Flop Proc (.clk(CLK), .D(or_4_out), .Q(Proc_q), .reset(or_10_out));  // open: Qn, preset, en
  or or_10 (or_10_out, ~Chip_Select, Reset);  // OR_Gate
  Demultiplexer #(.enable("false")) demultiplexer_2 (
    .out0(Count), .out1(Update_Mem), .in(demultiplexer_3_out0), .sel(Zero_Time));
  Demultiplexer #(.enable("false")) demultiplexer_3 (
    .out0(demultiplexer_3_out0), .out1(Load1), .in(Proc_q), .sel(Changed));
  Clock clock_1 (.out(CLK));
  Comparator #(.width(32)) comparator_2 (.a(register_1_q), .b(Data_In_0), .eq(comparator_2_eq));  // open: gt, lt
  Comparator #(.width(32)) comparator_3 (.a(register_2_q), .b(Data_In_1), .eq(comparator_3_eq));  // open: gt, lt
  Comparator #(.width(32)) comparator_4 (.a(register_3_q), .b(Data_In_2), .eq(comparator_4_eq));  // open: gt, lt
  Comparator #(.width(32)) comparator_5 (.a(register_4_q), .b(Data_In_3), .eq(comparator_5_eq));  // open: gt, lt
  Comparator #(.width(32)) comparator_6 (
    .a(register_5_q), .b({{11{1'b1}}, nRead_Write, Mask, in_1}), .eq(comparator_6_eq));  // open: gt, lt
  nand nand_1 (nand_1_out, comparator_6_eq, comparator_2_eq, comparator_3_eq, comparator_4_eq, comparator_5_eq);
  and and_1 (Changed, nand_1_out, Chip_Select);
  or or_11 (Load, Count, Load1, Load0);
  and and_2 (and_2_out, Mask[0], Update_Mem, nRead_Write);
  and and_3 (and_3_out, Mask[1], Update_Mem, nRead_Write);
  and and_4 (and_4_out, Mask[2], Update_Mem, nRead_Write);
  and and_5 (and_5_out, Mask[3], Update_Mem, nRead_Write);
  RAM_part #(.addrWidth(16), .dataWidth(32), .bus("separate")) ram_1 (
    .addr(in_1), .din(Data_In_0), .data(Data_Out_0), .str(and_2_out), .sel(Chip_Select), .clk(CLK),
    .ld(and_6_out), .clr(Reset));
  and and_6 (and_6_out, ~nRead_Write, Idle);  // AND_Gate
  RAM_part #(.addrWidth(16), .dataWidth(32), .bus("separate")) ram_2 (
    .addr(in_1), .din(Data_In_1), .data(Data_Out_1), .str(and_3_out), .sel(Chip_Select), .clk(CLK),
    .ld(and_7_out), .clr(Reset));
  and and_7 (and_7_out, ~nRead_Write, Idle);  // AND_Gate
  RAM_part #(.addrWidth(16), .dataWidth(32), .bus("separate")) ram_3 (
    .addr(in_1), .din(Data_In_2), .data(Data_Out_2), .str(and_4_out), .sel(Chip_Select), .clk(CLK),
    .ld(and_8_out), .clr(Reset));
  and and_8 (and_8_out, ~nRead_Write, Idle);  // AND_Gate
  RAM_part #(.addrWidth(16), .dataWidth(32), .bus("separate")) ram_4 (
    .addr(in_1), .din(Data_In_3), .data(Data_Out_3), .str(and_5_out), .sel(Chip_Select), .clk(CLK),
    .ld(and_9_out), .clr(Reset));
  and and_9 (and_9_out, ~nRead_Write, Idle);  // AND_Gate

  assign Read_Time = 4'b0011;
  assign Write_Time = 4'b0010;

  // Other names for the same wires on the sheet: Address[15:0] = in_1; M0 = Mask[0]; M1 = Mask[1]; M2 = Mask[2];
  //   M3 = Mask[3]; RW = nRead_Write; CLR = Reset; CS = Chip_Select; Load2 = Count

  // Notes on the sheet:
  //   NO MODIFICAR
  //   excepto quizás los valores RT y WT
  //   BANK0
  //   BANK1
  //   BANK2
  //   BANK3
endmodule

module S_MIPS (
  input  [31:0] RAM_Out_0,
  input  [31:0] RAM_Out_1,
  input  Reset,
  input  Clock,
  input  [31:0] RAM_Out_2,
  input  [31:0] RAM_Out_3,
  input  Kbd_Available,
  input  [6:0] Kbd_ASCII_Data,
  input  [3:0] Read_Time,
  input  [3:0] Write_Time,
  output [15:0] Address,
  output Kbd_Enable,
  output Kbd_Clear,
  output TTY_Enable,
  output [31:0] RAM_In_0,
  output [6:0] TTY_ASCII_Data,
  output [31:0] RAM_In_1,
  output Stop,
  output [31:0] RAM_In_2,
  output [31:0] RAM_In_3,
  output [3:0] Mask,
  output nRead_Write,
  output Chip_Select
);

  wire Add, Addi, And, Andi, Beq, Bgtz, Blez, Bltz, Bne, Div, Divu, Finished, Get_Instruction, GetJump, Jr,
       Jump, Kbd, Lw, Lw1, Mfhi, Mflo, Mult, multiplexer_1_out, multiplexer_2_out, Mulu, Next, Nop, Nor, Or,
       or_1_out, or_2_out, or_3_out, Ori, Pop, Pop1, Push, RD, Read_Ram_1, Read_Ram_2, Ready, RF_E, Rnd,
       RRam, Slt, Slti, Sltiu, Sltu, SPEnable, SPpop, Sub, Sw, Tty, Write_Ram, Xor, Xori;
  wire [1:0] Block;
  wire [2:0] BrachSelector;
  wire [3:0] Instruction_ALU;
  wire [4:0] data_address_1_output_address, Rd_t, Rs_t, Rt_t, X;
  wire [7:0] pc_1_block_2;
  wire [7:2] pc_1_block;
  wire [15:0] Offset;
  wire [25:0] Destination;
  wire [31:0] A, control_unity_1_data_from_ram, data_input_1_data_output, Hi_Output, Hi_OUTPUT_t,
       kbd_1_output, LO_OUTPUT, Lo_Output_t, ls_sw_push_1_raminput0, multiplexer_3_out, NextInstruccion, PC,
       Ram_Addres, register_1_q, ResultAlu, rnd_Content, RT, Sltiu_slti_Content, SP;
  wire [31:7] RS;

  or or_1 (or_1_out, Mulu, Divu, Slt, Sltiu);
  Multiplexer multiplexer_1 (.in0(RS[31]), .in1(1'b0), .out(multiplexer_1_out), .sel(or_1_out));  // open: en
  Multiplexer multiplexer_2 (.in0(A[31]), .in1(1'b0), .out(multiplexer_2_out), .sel(or_1_out));  // open: en
  // Probe on TTY_ASCII_Data
  Reading_Writing_Ram reading_writing_ram_1 (
    .Read_Time(Read_Time), .Write_Time(Write_Time), .Ready(Ready), .Finished(Finished),
    .Read_Ram_1(Read_Ram_1), .Write_Ram(Write_Ram), .Read_Ram_2(Read_Ram_2));
  PC pc_1 (
    .Block({pc_1_block_2, pc_1_block, Block}), .RAM_A(Address), .PC(PC), .CLR(Reset), .SP(SP), .Next(Next),
    .Jump(NextInstruccion), .GetJump(GetJump), .Rw(nRead_Write), .RRam(RRam), .Ram_Addres(Ram_Addres),
    .LW(Lw), .SW(Sw));
  KBD kbd_1 (.in_1(Kbd_ASCII_Data), .Output(kbd_1_output), .KbdAvaliable(Kbd_Available));
  ALU alu_1 (
    .Instruction(Instruction_ALU), .Rs({RS, TTY_ASCII_Data}), .Rt(A), .Rs_Signed(multiplexer_1_out),
    .Rt_Signed(multiplexer_2_out), .Output(ResultAlu), .Hi_Output(Hi_Output), .Lo_Output(Lo_Output_t),
    .Sltu(Sltu));
  Multiplexer #(.select(2), .width(32)) multiplexer_3 (
    .in0(RAM_Out_0), .in1(RAM_Out_1), .in2(RAM_Out_2), .in3(RAM_Out_3), .out(multiplexer_3_out), .sel(Block));  // open: en
  or or_2 (or_2_out, Sltiu, Slti);
  DATA_INPUT data_input_1 (
    .RAM_OUTPUT_0(multiplexer_3_out), .ResoultAlu(ResultAlu), .Lw1(Lw1), .CLR(Reset), .Push(Push),
    .DATA_OUTPUT(data_input_1_data_output), .Pop1(Pop1), .Lo_Output(LO_OUTPUT), .Hi_Output(Hi_OUTPUT_t),
    .Mflo(Mflo), .Mfhi(Mfhi), .Slti_Sltiu(Sltiu_slti_Content), .sltiu_slti(or_2_out), .rnd_2(rnd_Content),
    .rnd(Rnd), .Kbd(Kbd), .KbdData(kbd_1_output));
  DATA_ADDRESS data_address_1 (
    .Rt(Rt_t), .Rd(Rd_t), .RD_2(RD), .Output_ADDRESS(data_address_1_output_address), .Lw(Lw), .CLR(Reset),
    .rnd(Rnd), .Pop(Pop), .Pop1(Pop1), .Lw1(Lw1));
  LS_SW_PUSH ls_sw_push_1 (
    .RAMInput0(ls_sw_push_1_raminput0), .OFFSET(Offset), .in_2({RS, TTY_ASCII_Data}), .in_3(RT), .PUSH(Push),
    .SW(Sw), .RAMAddress(Ram_Addres));
  Demultiplexer #(.select(2), .width(32)) demultiplexer_1 (
    .out0(RAM_In_0), .out1(RAM_In_1), .out2(RAM_In_2), .out3(RAM_In_3), .in(ls_sw_push_1_raminput0),
    .sel(Block));  // open: en
  BranchControl branchcontrol_1 (
    .in_1(BrachSelector), .RS({RS, TTY_ASCII_Data}), .RT(RT), .in_4(PC), .OFSSET(Offset),
    .Destination(Destination), .Salida(NextInstruccion));
  Control_Unity control_unity_1 (
    .Input_Ram_0(RAM_Out_0), .Input_Ram_1(RAM_Out_1), .Input_Ram_2(RAM_Out_2), .Input_Ram_3(RAM_Out_3),
    .Block({pc_1_block_2, pc_1_block, Block}), .Mask(Mask), .Data_from_Ram(control_unity_1_data_from_ram));
  RF rf_1 (
    .Data_Input(data_input_1_data_output), .Destination_Adrres(data_address_1_output_address),
    .Input_Hi(Hi_Output), .Input_Lo(Lo_Output_t), .RA(Rt_t), .RB(Rs_t), .RW(RF_E), .Enable(RF_E),
    .Enable_Hi(or_3_out), .Enable_Lo(or_3_out), .Reset(Reset), .Register_A(RT),
    .Register_B({RS, TTY_ASCII_Data}), .Hi_Output(Hi_OUTPUT_t), .Lo_Output(LO_OUTPUT), .SP(SP), .Push(Push),
    .SPenable(SPEnable));
  or or_3 (or_3_out, Mult, Mulu, Div, Divu);
  Register #(.width(32)) register_1 (
    .D(control_unity_1_data_from_ram), .Q(register_1_q), .clk(Clock));  // open: en, clr
  InstructionDecoder instructiondecoder_1 (
    .Instruction(register_1_q), .Nop(Nop), .Add(Add), .Sub(Sub), .Mult(Mult), .Mulu(Mulu), .Div(Div),
    .Divu(Divu), .Slt(Slt), .Sltu(Sltu), .And(And), .Or(Or), .Nor(Nor), .XOr(Xor), .Addi(Addi), .Slti(Slti),
    .Sltiu(Sltiu), .Andi(Andi), .Ori(Ori), .XOri(Xori), .Lw(Lw), .Sw(Sw), .Pop(Pop), .Push(Push), .Beq(Beq),
    .Bne(Bne), .Blez(Blez), .Bgtz(Bgtz), .Bltz(Bltz), .Jump(Jump), .Jr(Jr), .Mfhi(Mfhi), .Mflo(Mflo),
    .Halt(Stop), .Tty(Tty), .Rnd(Rnd), .Kbd(Kbd), .Instruccion_ALU(Instruction_ALU), .X(X), .Rd(Rd_t),
    .Rt(Rt_t), .Rs(Rs_t), .Constante(Offset), .JumpCode(BrachSelector), .Destination(Destination));
  DATA_PATH data_path_1 (
    .Add(Add), .Sub(Sub), .Mflo(Mflo), .Mfhi(Mfhi), .Pop(Pop), .Slt(Slt), .Sltu(Sltu), .And(And), .Nor(Nor),
    .Xor(Xor), .Addi(Addi), .Slti(Slti), .Sltiu(Sltiu), .Or(Or), .Andi(Andi), .Ori(Ori), .Xori(Xori),
    .Beq(Beq), .Blez(Blez), .Bgtz(Bgtz), .Bltz(Bltz), .Jump(Jump), .Jr(Jr), .KBD_CLR(Kbd_Clear),
    .Get_Instruction(Get_Instruction), .Nop(Nop), .Lw(Lw), .Sw(Sw), .Push(Push), .Read_Ram_1(Read_Ram_1),
    .Finished(Finished), .Write_Ram(Write_Ram), .RW(nRead_Write), .Halt(Stop), .Next(Next), .Bne(Bne),
    .RF_E(RF_E), .CLR(Reset), .GetJump(GetJump), .TTY_ENABLE(TTY_Enable), .Tty(Tty), .Read_Ram_2(Read_Ram_2),
    .Ready(Ready), .rnd(Rnd), .RRam(RRam), .SPpop(SPpop), .SPEnable(SPEnable), .Pop1(Pop1), .Lw1(Lw1),
    .Kbd(Kbd), .Kbd_Enable(Kbd_Enable));
  Useful useful_1 (
    .Offset(Offset), .RS({RS, TTY_ASCII_Data}), .Rd(rnd_Content), .Rt(Sltiu_slti_Content), .sltiu(Sltiu));  // open: Trigger
  Utilities utilities_1 (
    .Offset(Offset), .RT(RT), .Mflo(Mflo), .Add(Add), .Sub(Sub), .Mult(Mult), .Mulu(Mulu), .Div(Div),
    .Divu(Divu), .Slt(Slt), .Sltu(Sltu), .And(And), .Xor(Xor), .Nor(Nor), .Mfhi(Mfhi), .A(A), .RD(RD),
    .OR(Or), .Kbd(Kbd));

  assign Chip_Select = 1'b1;

  // Other names for the same wires on the sheet: CLK = Clock; CLR = Reset; Halt = Stop; KBD_AVAIL = Kbd_Available;
  //   KBD_CLR = Kbd_Clear; KBD_DATA[6:0] = Kbd_ASCII_Data; RAM_A[15:0] = Address; RAM_INPUT_0[31:0] = RAM_In_0;
  //   RAM_INPUT_1[31:0] = RAM_In_1; RAM_INPUT_2[31:0] = RAM_In_2; RAM_INPUT_3[31:0] = RAM_In_3; RAM_MASK[3:0] = Mask;
  //   RAM_OUTPUT_0[31:0] = RAM_Out_0; RAM_OUTPUT_1[31:0] = RAM_Out_1; RAM_OUTPUT_2[31:0] = RAM_Out_2;
  //   RAM_OUTPUT_3[31:0] = RAM_Out_3; RS[6:0] = TTY_ASCII_Data; TTY_DATA[6:0] = TTY_ASCII_Data; RW = nRead_Write

  // Notes on the sheet:
  //   DATA TO RAM
  //   DATA FROM RAM
  //   DATA WRITE MASK
  //   RAM TIMING
  //   RAM CONTROL
  //   UNSIGNED
  //   RAM ADDRESS
  //   SEQUENCING
  //   KEYBOARD
  //   TTY
  //   Architecture
  //   S-Mips
endmodule

module RAM_Dispatcher (
  input  [3:0] WriteTime,
  input  Clock,
  input  CLR,
  output [31:0] Data,
  output [15:0] Address,
  output [3:0] Mask,
  output Finished,
  output Write
);

  wire demultiplexer_2_out1, demultiplexer_3_out1, End, IDLE_q, IncAddr, Load, or_1_out, or_2_out, While_q,
       WriteEnd;
  wire [3:0] counter_1_q;
  wire [31:0] CurrentAddress_q;

  Counter #(.width(32), .max('hffffffff)) CurrentAddress (
    .count(IncAddr), .Q({CurrentAddress_q[31:18], Address, CurrentAddress_q[1:0]}), .clk(Clock), .clr(CLR));  // open: load, D, carry
  or or_1 (or_1_out, IncAddr, demultiplexer_3_out1, Finished);
  D_Flip_Flop IDLE (.clk(Clock), .D(or_1_out), .Q(IDLE_q), .preset(CLR));  // open: Qn, en, reset
  Demultiplexer #(.enable("false")) demultiplexer_1 (.out0(Load), .out1(Finished), .in(IDLE_q), .sel(End));
  D_Flip_Flop While (.clk(Clock), .D(or_2_out), .Q(While_q), .reset(CLR));  // open: Qn, preset, en
  or or_2 (or_2_out, Write, Load);
  RAM_part #(.addrWidth(18), .dataWidth(32)) ram_1 (
    .addr({Address, CurrentAddress_q[1:0]}), .data(Data), .clk(Clock));  // open: sel, ld, clr
  Demultiplexer #(.enable("false")) demultiplexer_2 (
    .out0(Write), .out1(demultiplexer_2_out1), .in(While_q), .sel(WriteEnd));
  Decoder #(.select(2)) decoder_1 (
    .out0(Mask[0]), .out1(Mask[1]), .out2(Mask[2]), .out3(Mask[3]), .sel(CurrentAddress_q[1:0]));  // open: en
  Demultiplexer #(.enable("false")) demultiplexer_3 (
    .out0(IncAddr), .out1(demultiplexer_3_out1), .in(demultiplexer_2_out1), .sel(End));
  Counter #(.width(4), .max('hf)) counter_1 (
    .load(Load), .D(WriteTime), .count(Write), .Q(counter_1_q), .clk(Clock));  // open: carry, clr
  Comparator #(.width(32)) comparator_1 (.a(Data), .b({32{1'b1}}), .eq(End));  // open: gt, lt
  Comparator #(.width(4)) comparator_2 (.a(4'b0000), .b(counter_1_q), .eq(WriteEnd));  // open: gt, lt

  // Other names for the same wires on the sheet: CLK = Clock; Count = Write; WT[3:0] = WriteTime
endmodule

module ALU (
  input  [3:0] Instruction,
  input  [31:0] Rs,
  input  Sltu,
  input  [31:0] Rt,
  input  Rs_Signed,
  input  Rt_Signed,
  output [31:0] Output,
  output [31:0] Hi_Output,
  output [31:0] Lo_Output
);

  wire adder_1_cout, Invert, or_1_out, subtractor_1_bout;
  wire [0:0] Rs_Rt;
  wire [31:0] AddResult, and_3_out, divider_1_out, divider_2_out, divider_3_out, divider_4_out, DivResult,
       multiplexer_1_out, multiplexer_2_out, MultRemains, MultResult, negator_1_out, negator_2_out, Not_Rs,
       or_3_out, Remains, Remains_1, Remains_2, Remains_2_Positive, Remains_3, Remains_3_Positive, Remains_4,
       Remains_4_Positive, Rs_AND_Rt, Rs_NAND_Rt, Rs_NOR_Rt, Rs_OR_Rt, Rs_t_t, Rs_XNOR_Rt, Rs_XOR_Rt, Rt_t_t,
       SubResult, subtractor_3_out, xor_2_out;

  // Probe on Rs
  or or_1 (or_1_out, Rt_Signed, Rs_Signed);
  and and_1 (Invert, Rs[31], ~Rt[31], ~or_1_out);  // AND_Gate
  // Probe on Rt
  Adder #(.width(32)) adder_1 (.a(Rs), .b(Rt), .out(AddResult), .cout(adder_1_cout));  // open: cin
  Subtractor #(.width(32)) subtractor_1 (.a(Rs), .b(Rt), .out(SubResult), .bout(subtractor_1_bout));  // open: bin
  Multiplier #(.width(32)) multiplier_1 (.a(Rs), .b(Rt), .out(MultResult), .cout(MultRemains));  // open: cin
  Divider #(.width(32)) divider_1 (.a(Rs), .b(Rt), .out(divider_1_out), .rem(Remains_1));  // open: upper
  Divider #(.width(32)) divider_2 (.a(Rs_t_t), .b(Rt), .out(divider_2_out), .rem(Remains_2));  // open: upper
  Divider #(.width(32)) divider_3 (.a(Rs), .b(Rt_t_t), .out(divider_3_out), .rem(Remains_3));  // open: upper
  Divider #(.width(32)) divider_4 (.a(Rs_t_t), .b(Rt_t_t), .out(divider_4_out), .rem(Remains_4));  // open: upper
  Negator #(.width(32)) negator_1 (.in(divider_2_out), .out(negator_1_out));
  Negator #(.width(32)) negator_2 (.in(divider_3_out), .out(negator_2_out));
  Multiplexer #(.width(32)) multiplexer_1 (
    .in0(Rs), .in1({1'b0, Rs[30:0]}), .out(multiplexer_1_out), .sel(Sltu));  // open: en
  Multiplexer #(.width(32)) multiplexer_2 (
    .in0(Rt), .in1({1'b0, Rt[30:0]}), .out(multiplexer_2_out), .sel(Sltu));  // open: en
  Multiplexer #(.select(2), .width(32)) multiplexer_3 (
    .in0(divider_1_out), .in1(negator_1_out), .in2(negator_2_out), .in3(divider_4_out), .out(DivResult),
    .sel({Rt_Signed, Rs_Signed}));  // open: en
  Comparator #(.width(32)) comparator_1 (.a(multiplexer_1_out), .b(multiplexer_2_out), .lt(Rs_Rt[0]));  // open: gt, eq
  Negator #(.width(32)) negator_3 (.in(Rs), .out(Rs_t_t));
  Negator #(.width(32)) negator_4 (.in(Rt), .out(Rt_t_t));
  assign Rs_AND_Rt = Rs & Rt;  // AND_Gate and_2, 32 bits wide
  assign and_3_out = Rs & Rt;  // AND_Gate and_3, 32 bits wide
  assign Rs_NAND_Rt = ~and_3_out;  // NOT_Gate not_1, 32 bits wide
  assign Rs_OR_Rt = Rs | Rt;  // OR_Gate or_2, 32 bits wide
  assign or_3_out = Rs | Rt;  // OR_Gate or_3, 32 bits wide
  assign Rs_NOR_Rt = ~or_3_out;  // NOT_Gate not_2, 32 bits wide
  assign Rs_XOR_Rt = Rs ^ Rt;  // XOR_Gate xor_1, 32 bits wide
  assign Rs_XNOR_Rt = ~xor_2_out;  // NOT_Gate not_3, 32 bits wide
  assign xor_2_out = Rs ^ Rt;  // XOR_Gate xor_2, 32 bits wide
  assign Not_Rs = ~Rs;  // NOT_Gate not_4, 32 bits wide
  Subtractor #(.width(32)) subtractor_2 (.a(Rt), .b(Remains_2), .out(Remains_2_Positive));  // open: bin, bout
  Subtractor #(.width(32)) subtractor_3 (.a(Rt_t_t), .b(Remains_3), .out(subtractor_3_out));  // open: bin, bout
  Subtractor #(.width(32)) subtractor_4 (.a(Rt_t_t), .b(Remains_4), .out(Remains_4_Positive));  // open: bin, bout
  Multiplexer #(.select(4), .width(32)) multiplexer_4 (
    .in0(AddResult), .in1(SubResult), .in6({{31{1'b0}}, Rs_Rt[0]}), .in7(Remains), .in8(Rs_AND_Rt),
    .in9(Rs_NAND_Rt), .in10(Rs_OR_Rt), .in11(Rs_NOR_Rt), .in12(Rs_XOR_Rt), .in13(Rs_XNOR_Rt), .in14(Not_Rs),
    .in15(Rs_t_t), .out(Output), .sel(Instruction));  // open: in2, in3, in4, in5, en
  Multiplexer #(.select(4), .width(32)) multiplexer_5 (
    .in0({32{1'b0}}), .in1({32{1'b0}}), .in2(MultRemains), .in3(Remains), .in4({32{1'b0}}), .in5({32{1'b0}}),
    .in6({32{1'b0}}), .in7({32{1'b0}}), .in8({32{1'b0}}), .in9({32{1'b0}}), .in10({32{1'b0}}),
    .in11({32{1'b0}}), .in12({32{1'b0}}), .in13({32{1'b0}}), .in14({32{1'b0}}), .in15({32{1'b0}}),
    .out(Hi_Output), .sel(Instruction));  // open: en
  Multiplexer #(.select(4), .width(32)) multiplexer_6 (
    .in0({32{1'b0}}), .in1({32{1'b0}}), .in2(MultResult), .in3(DivResult), .in4({32{1'b0}}),
    .in5({32{1'b0}}), .in6({32{1'b0}}), .in7({32{1'b0}}), .in8({32{1'b0}}), .in9({32{1'b0}}),
    .in10({32{1'b0}}), .in11({32{1'b0}}), .in12({32{1'b0}}), .in13({32{1'b0}}), .in14({32{1'b0}}),
    .in15({32{1'b0}}), .out(Lo_Output), .sel(Instruction));  // open: en
  Multiplexer #(.select(2), .width(32)) multiplexer_7 (
    .in0(Remains_1), .in1(Remains_2), .in2(Remains_3), .in3(Remains_4), .out(Remains),
    .sel({Rt_Signed, Rs_Signed}));  // open: en
  Subtractor #(.width(32)) subtractor_5 (
    .a(Rt_t_t), .b(subtractor_3_out), .out(Remains_3_Positive));  // open: bin, bout

  // Other names for the same wires on the sheet: DivSelector[1:0] = {Rt_Signed, Rs_Signed}; Result[31:0] = Output;
  //   Rs_t[30:0] = Rs[30:0]; Rt_t[30:0] = Rt[30:0]

  // Notes on the sheet:
  //   Rs_Signed
  //   Rt_Signed
  //   Both_Unsigned
  //   Both_Signed
  //   Comparadores
  //   Moduladores de Rs y Rt
  //   Operaciones Logicas
  //   Restos positivos de la division
  //   Salidas
endmodule

module RF (
  input  [31:0] Data_Input,
  input  [4:0] Destination_Adrres,
  input  [31:0] Input_Hi,
  input  [31:0] Input_Lo,
  input  [4:0] RA,
  input  [4:0] RB,
  input  RW,
  input  Enable,
  input  Enable_Hi,
  input  Enable_Lo,
  input  Reset,
  input  Push,
  input  SPenable,
  output [31:0] Register_A,
  output [31:0] Register_B,
  output [31:0] Hi_Output,
  output [31:0] Lo_Output,
  output [31:0] SP
);

  wire and_1_out, Clock, Enable_0, Enable_1, Enable_2, Enable_3, Enable_4, Enable_5, Enable_6, Enable_7,
       Enable_8, Enable_9, Enable_10, Enable_11, Enable_12, Enable_13, Enable_14, Enable_15, Enable_16,
       Enable_17, Enable_18, Enable_19, Enable_20, Enable_21, Enable_22, Enable_23, Enable_24, Enable_25,
       Enable_26, Enable_27, Enable_28, Enable_29, Enable_30, Enable_31, or_1_out;
  wire [31:0] multiplexer_1_out, multiplexer_2_out, NewSP, R0, R0_Input, R1, R1_Input, R2, R2_Input, R3,
       R3_Input, R4, R4_Input, R5, R5_Input, R6, R6_Input, R7, R7_Input, R8, R8_Input, R9, R9_Input, R10,
       R10_Input, R11, R11_Input, R12, R12_Input, R13, R13_Input, R14, R14_Input, R15, R15_Input, R16,
       R16_Input, R17, R17_Input, R18, R18_Input, R19, R19_Input, R20, R20_Input, R21, R21_Input, R22,
       R22_Input, R23, R23_Input, R24, R24_Input, R25, R25_Input, R26, R26_Input, R27, R27_Input, R28,
       R28_Input, R29, R29_Input, R30, R30_Input, R31, R31_Input;

  Clock clock_1 (.out(Clock));
  Register #(.width(32)) u_R0 (.D(R0_Input), .en(1'b0), .Q(R0), .clk(Clock), .clr(Reset));
  Register #(.width(32)) u_R1 (.D(R1_Input), .en(Enable_1), .Q(R1), .clk(Clock), .clr(Reset));
  // Probe on R8
  Register #(.width(32)) u_R8 (.D(R8_Input), .en(Enable_8), .Q(R8), .clk(Clock), .clr(Reset));
  Register #(.width(32)) u_R9 (.D(R9_Input), .en(Enable_9), .Q(R9), .clk(Clock), .clr(Reset));
  Register #(.width(32)) u_R16 (.D(R16_Input), .en(Enable_16), .Q(R16), .clk(Clock), .clr(Reset));
  Register #(.width(32)) u_R17 (.D(R17_Input), .en(Enable_17), .Q(R17), .clk(Clock), .clr(Reset));
  Register #(.width(32)) u_R24 (.D(R24_Input), .en(Enable_24), .Q(R24), .clk(Clock), .clr(Reset));
  Register #(.width(32)) u_R25 (.D(R25_Input), .en(Enable_25), .Q(R25), .clk(Clock), .clr(Reset));
  // Probe on R0
  // Probe on R1
  Register #(.width(32)) u_R2 (.D(R2_Input), .en(Enable_2), .Q(R2), .clk(Clock), .clr(Reset));
  Register #(.width(32)) u_R3 (.D(R3_Input), .en(Enable_3), .Q(R3), .clk(Clock), .clr(Reset));
  Register #(.width(32)) u_R10 (.D(R10_Input), .en(Enable_10), .Q(R10), .clk(Clock), .clr(Reset));
  Register #(.width(32)) u_R11 (.D(R11_Input), .en(Enable_11), .Q(R11), .clk(Clock), .clr(Reset));
  Register #(.width(32)) u_R18 (.D(R18_Input), .en(Enable_18), .Q(R18), .clk(Clock), .clr(Reset));
  Register #(.width(32)) u_R19 (.D(R19_Input), .en(Enable_19), .Q(R19), .clk(Clock), .clr(Reset));
  Register #(.width(32)) u_R26 (.D(R26_Input), .en(Enable_26), .Q(R26), .clk(Clock), .clr(Reset));
  Register #(.width(32)) u_R27 (.D(R27_Input), .en(Enable_27), .Q(R27), .clk(Clock), .clr(Reset));
  // Probe on R2
  // Probe on R3
  Multiplexer #(.width(32)) multiplexer_1 (
    .in0(32'h4), .in1(32'hfffffffc), .out(multiplexer_1_out), .sel(Push));  // open: en
  Register #(.width(32)) u_R4 (.D(R4_Input), .en(Enable_4), .Q(R4), .clk(Clock), .clr(Reset));
  Register #(.width(32)) u_R5 (.D(R5_Input), .en(Enable_5), .Q(R5), .clk(Clock), .clr(Reset));
  Register #(.width(32)) u_R20 (.D(R20_Input), .en(Enable_20), .Q(R20), .clk(Clock), .clr(Reset));
  Register #(.width(32)) u_R21 (.D(R21_Input), .en(Enable_21), .Q(R21), .clk(Clock), .clr(Reset));
  Register #(.width(32)) u_R28 (.D(R28_Input), .en(Enable_28), .Q(R28), .clk(Clock), .clr(Reset));
  Register #(.width(32)) u_R29 (.D(R29_Input), .en(Enable_29), .Q(R29), .clk(Clock), .clr(Reset));
  Register #(.width(32)) u_R12 (.D(R12_Input), .en(Enable_12), .Q(R12), .clk(Clock), .clr(Reset));
  Register #(.width(32)) u_R13 (.D(R13_Input), .en(Enable_13), .Q(R13), .clk(Clock), .clr(Reset));
  Adder #(.width(32)) adder_1 (.a(multiplexer_1_out), .b(SP), .out(NewSP));  // open: cin, cout
  // Probe on R4
  // Probe on R5
  Register #(.width(32)) u_R22 (.D(R22_Input), .en(Enable_22), .Q(R22), .clk(Clock), .clr(Reset));
  Register #(.width(32)) u_R23 (.D(R23_Input), .en(Enable_23), .Q(R23), .clk(Clock), .clr(Reset));
  Register #(.width(32)) u_R30 (.D(R30_Input), .en(Enable_30), .Q(R30), .clk(Clock), .clr(Reset));
  Multiplexer #(.width(32)) multiplexer_2 (
    .in0(R31_Input), .in1(NewSP), .out(multiplexer_2_out), .sel(SPenable));  // open: en
  or or_1 (or_1_out, Enable_31, SPenable);
  Register #(.width(32)) u_R6 (.D(R6_Input), .en(Enable_6), .Q(R6), .clk(Clock), .clr(Reset));
  Register #(.width(32)) u_R7 (.D(R7_Input), .en(Enable_7), .Q(R7), .clk(Clock), .clr(Reset));
  Register #(.width(32)) u_R31 (.D(multiplexer_2_out), .en(or_1_out), .Q(SP), .clk(Clock), .clr(Reset));
  // Probe on R6
  Register #(.width(32)) u_R14 (.D(R14_Input), .en(Enable_14), .Q(R14), .clk(Clock), .clr(Reset));
  Register #(.width(32)) u_R15 (.D(R15_Input), .en(Enable_15), .Q(R15), .clk(Clock), .clr(Reset));
  // Probe on R7
  Register #(.width(32)) Hi_Register (.D(Input_Hi), .en(Enable_Hi), .Q(Hi_Output), .clk(Clock), .clr(Reset));
  Register #(.width(32)) Lo_Register (.D(Input_Lo), .en(Enable_Lo), .Q(Lo_Output), .clk(Clock), .clr(Reset));
  Demultiplexer #(.select(5), .width(32)) demultiplexer_1 (
    .out0(R0_Input), .out1(R1_Input), .out2(R2_Input), .out3(R3_Input), .out4(R4_Input), .out5(R5_Input),
    .out6(R6_Input), .out7(R7_Input), .out8(R8_Input), .out9(R9_Input), .out10(R10_Input), .out11(R11_Input),
    .out12(R12_Input), .out13(R13_Input), .out14(R14_Input), .out15(R15_Input), .out16(R16_Input),
    .out17(R17_Input), .out18(R18_Input), .out19(R19_Input), .out20(R20_Input), .out21(R21_Input),
    .out22(R22_Input), .out23(R23_Input), .out24(R24_Input), .out25(R25_Input), .out26(R26_Input),
    .out27(R27_Input), .out28(R28_Input), .out29(R29_Input), .out30(R30_Input), .out31(R31_Input),
    .in(Data_Input), .sel(Destination_Adrres), .en(RW));
  Demultiplexer #(.select(5)) demultiplexer_2 (
    .out0(Enable_0), .out1(Enable_1), .out2(Enable_2), .out3(Enable_3), .out4(Enable_4), .out5(Enable_5),
    .out6(Enable_6), .out7(Enable_7), .out8(Enable_8), .out9(Enable_9), .out10(Enable_10), .out11(Enable_11),
    .out12(Enable_12), .out13(Enable_13), .out14(Enable_14), .out15(Enable_15), .out16(Enable_16),
    .out17(Enable_17), .out18(Enable_18), .out19(Enable_19), .out20(Enable_20), .out21(Enable_21),
    .out22(Enable_22), .out23(Enable_23), .out24(Enable_24), .out25(Enable_25), .out26(Enable_26),
    .out27(Enable_27), .out28(Enable_28), .out29(Enable_29), .out30(Enable_30), .out31(Enable_31),
    .in(Enable), .sel(Destination_Adrres), .en(and_1_out));
  and and_1 (and_1_out, ~Enable_Hi, ~Enable_Lo, RW);  // AND_Gate
  // Probe on Hi_Output
  // Probe on Lo_Output
  Multiplexer #(.select(5), .width(32)) multiplexer_3 (
    .in0(R0), .in1(R1), .in2(R2), .in3(R3), .in4(R4), .in5(R5), .in6(R6), .in7(R7), .in8(R8), .in9(R9),
    .in10(R10), .in11(R11), .in12(R12), .in13(R13), .in14(R14), .in15(R15), .in16(R16), .in17(R17),
    .in18(R18), .in19(R19), .in20(R20), .in21(R21), .in22(R22), .in23(R23), .in24(R24), .in25(R25),
    .in26(R26), .in27(R27), .in28(R28), .in29(R29), .in30(R30), .in31(R31), .out(Register_A), .sel(RA));  // open: en
  Multiplexer #(.select(5), .width(32)) multiplexer_4 (
    .in0(R0), .in1(R1), .in2(R2), .in3(R3), .in4(R4), .in5(R5), .in6(R6), .in7(R7), .in8(R8), .in9(R9),
    .in10(R10), .in11(R11), .in12(R12), .in13(R13), .in14(R14), .in15(R15), .in16(R16), .in17(R17),
    .in18(R18), .in19(R19), .in20(R20), .in21(R21), .in22(R22), .in23(R23), .in24(R24), .in25(R25),
    .in26(R26), .in27(R27), .in28(R28), .in29(R29), .in30(R30), .in31(SP), .out(Register_B), .sel(RB));  // open: en

  // Other names for the same wires on the sheet: Address[4:0] = Destination_Adrres; DataInput[31:0] = Data_Input;
  //   Hi[31:0] = Hi_Output; Lo[31:0] = Lo_Output; R31_SP[31:0] = SP
endmodule

module InstructionDecoder (
  input  [31:0] Instruction,
  output Nop,
  output Add,
  output Sub,
  output Mult,
  output Mulu,
  output Div,
  output Divu,
  output Slt,
  output Sltu,
  output And,
  output Or,
  output Nor,
  output XOr,
  output Addi,
  output Slti,
  output Sltiu,
  output [25:0] Destination,
  output Andi,
  output Ori,
  output XOri,
  output Lw,
  output Sw,
  output Pop,
  output Push,
  output Beq,
  output Bne,
  output Blez,
  output [2:0] JumpCode,
  output Bgtz,
  output Bltz,
  output Jump,
  output Jr,
  output Mfhi,
  output Mflo,
  output Halt,
  output Tty,
  output Rnd,
  output Kbd,
  output [3:0] Instruccion_ALU,
  output [4:0] X,
  output [4:0] Rd,
  output [4:0] Rt,
  output [4:0] Rs,
  output [15:0] Constante
);

  wire Add_t, Addi_t, and_1_out, and_2_out, and_6_out, and_7_out, and_8_out, And_t, Andi_t, Beq_t, Bgtz_t,
       Blez_t, Bltz_t, Bne_t, Div_t, Divu_t, Especial, Halt_t, Instruccion_I, Instruccion_J, Instruccion_R,
       Jr_t, Kbd_t, Lw_t, Mfhi_t, Mflo_t, Mult_t, Mulu_t, Nop_t, Nor_t, not_1_out, or_2_out, Or_t, Ori_t,
       Pop_t, Push_t, R_No_Esp, Rnd_t, Slt_t, Slti_t, Sltiu_t, Sltu_t, Sub_t, Sw_t, Tty_t, XOr_t, XOri_t;
  wire [3:0] ALU_I, Instruccion_ALU_t;
  wire [4:0] Rs_1, Rs_2, Rt_1, Rt_2;
  wire [5:0] instructiondecoder_r_1_func_code;

  and and_1 (and_1_out, ~Instruction[2], ~Instruction[3], ~Instruction[4], ~Instruction[5], ~Instruction[6], ~Instruction[7]);  // AND_Gate
  and and_2 (and_2_out, ~Instruction[2], ~Instruction[3], ~Instruction[4], Instruction[5], Instruction[6], Instruction[7]);  // AND_Gate
  and and_3 (Especial, Instruction[2], Instruction[3], Instruction[4], Instruction[5], Instruction[6], Instruction[7]);
  and and_4 (Instruccion_J, ~Instruction[2], Instruction[3], ~Instruction[4], ~Instruction[5], ~Instruction[6], ~Instruction[7]);  // AND_Gate
  InstructionDecoder_I instructiondecoder_i_1 (
    .Instruction({Instruction[1:0], Instruction[15:8], Instruction[23:16], Instruction[31:24]}),
    .Operacion(Instruction[7:2]), .Constante(Constante), .Rt(Rt_2), .Rs(Rs_2), .Addi(Addi_t), .Slti(Slti_t),
    .Sltiu(Sltiu_t), .Andi(Andi_t), .Ori(Ori_t), .XOri(XOri_t), .Lw(Lw_t), .Sw(Sw_t), .Beq(Beq_t),
    .Bne(Bne_t), .Blez(Blez_t), .Bgtz(Bgtz_t), .Bltz(Bltz_t), .Instruction_2(ALU_I));
  or or_1 (Instruccion_R, and_1_out, Especial, and_2_out);
  InstructionDecoder_R instructiondecoder_r_1 (
    .Input({Instruction[1:0], Instruction[15:8], Instruction[23:16], Instruction[31:24]}),
    .Instruction(Instruccion_ALU_t), .X(X), .Rd(Rd), .Rt(Rt_1), .Rs(Rs_1),
    .Func_code(instructiondecoder_r_1_func_code), .No_operacion(Nop_t), .Add(Add_t), .Sub(Sub_t),
    .Mult(Mult_t), .Mulu(Mulu_t), .Div(Div_t), .Divu(Divu_t), .Slt(Slt_t), .Sltu(Sltu_t), .And(And_t),
    .Or(Or_t), .Nor(Nor_t), .XOr(XOr_t), .Push(Push_t), .Jr(Jr_t), .Mfhi(Mfhi_t), .Mflo(Mflo_t), .Pop(Pop_t));
  and and_5 (R_No_Esp, ~Especial, ~and_2_out, Instruccion_R);  // AND_Gate
  InstructionDecoder_R_Especial instructiondecoder_r_especial_1 (
    .Func_code(instructiondecoder_r_1_func_code), .Halt(Halt_t), .Tty(Tty_t), .Rnd(Rnd_t), .Kbd(Kbd_t));
  assign Instruccion_ALU = and_6_out ? ALU_I : 4'bz;  // Controlled_Buffer controlled_buffer_1
  and and_6 (and_6_out, ~Instruccion_R, ~Instruccion_J);  // AND_Gate
  nor nor_1 (Instruccion_I, Instruccion_J, Instruccion_R);
  and and_7 (and_7_out, ~Instruction[2], ~Instruction[3], ~Instruction[4], Instruction[5], Instruction[6], Instruction[7]);  // AND_Gate
  and and_8 (and_8_out, ~Instruction[2], ~Instruction[3], ~Instruction[4], Instruction[5], Instruction[6], Instruction[7]);  // AND_Gate
  or or_2 (or_2_out, Pop_t, Especial);
  assign Instruccion_ALU = or_2_out ? 4'b1111 : 4'bz;  // Controlled_Buffer controlled_buffer_2
  assign Instruccion_ALU = R_No_Esp ? Instruccion_ALU_t : 4'bz;  // Controlled_Buffer controlled_buffer_3
  assign Rt = Instruccion_R ? Rt_1 : 5'bz;  // Controlled_Buffer controlled_buffer_4
  not not_1 (not_1_out, Instruccion_R);
  assign Rs = Instruccion_R ? Rs_1 : 5'bz;  // Controlled_Buffer controlled_buffer_5
  and and_9 (Nop, R_No_Esp, Nop_t);
  and and_10 (Add, R_No_Esp, Add_t);
  and and_11 (Sub, R_No_Esp, Sub_t);
  and and_12 (Mult, R_No_Esp, Mult_t);
  and and_13 (Mulu, R_No_Esp, Mulu_t);
  and and_14 (Div, R_No_Esp, Div_t);
  and and_15 (Divu, R_No_Esp, Divu_t);
  and and_16 (Slt, R_No_Esp, Slt_t);
  and and_17 (Sltu, R_No_Esp, Sltu_t);
  and and_18 (And, R_No_Esp, And_t);
  and and_19 (Or, R_No_Esp, Or_t);
  and and_20 (Nor, R_No_Esp, Nor_t);
  and and_21 (XOr, R_No_Esp, XOr_t);
  and and_22 (Addi, Instruccion_I, Addi_t);
  and and_23 (Slti, Instruccion_I, Slti_t);
  and and_24 (Sltiu, Instruccion_I, Sltiu_t);
  and and_25 (Andi, Instruccion_I, Andi_t);
  and and_26 (Ori, Instruccion_I, Ori_t);
  and and_27 (XOri, Instruccion_I, XOri_t);
  and and_28 (Lw, Instruccion_I, Lw_t);
  and and_29 (Sw, Instruccion_I, Sw_t);
  and and_30 (Pop, Pop_t, and_7_out);
  and and_31 (Push, and_8_out, Push_t);
  and and_32 (Beq, Instruccion_I, Beq_t);
  and and_33 (Bne, Instruccion_I, Bne_t);
  and and_34 (Blez, Instruccion_I, Blez_t);
  and and_35 (Bgtz, Instruccion_I, Bgtz_t);
  and and_36 (Bltz, Instruccion_I, Bltz_t);
  and and_37 (Jump, Instruccion_J, Instruccion_J);
  and and_38 (Jr, Instruccion_R, Jr_t);
  and and_39 (Mfhi, Instruccion_R, Mfhi_t);
  and and_40 (Mflo, Instruccion_R, Mflo_t);
  and and_41 (Halt, Especial, Halt_t);
  and and_42 (Tty, Especial, Tty_t);
  and and_43 (Rnd, Especial, Rnd_t);
  and and_44 (Kbd, Especial, Kbd_t);
  assign Rt = not_1_out ? Rt_2 : 5'bz;  // Controlled_Buffer controlled_buffer_6
  assign Rs = not_1_out ? Rs_2 : 5'bz;  // Controlled_Buffer controlled_buffer_7
  assign JumpCode = Bltz_t ? 3'b100 : 3'bz;  // Controlled_Buffer controlled_buffer_8
  assign JumpCode = Instruccion_J ? 3'b101 : 3'bz;  // Controlled_Buffer controlled_buffer_9
  assign JumpCode = Jr_t ? 3'b110 : 3'bz;  // Controlled_Buffer controlled_buffer_10
  assign JumpCode = Beq_t ? 3'b000 : 3'bz;  // Controlled_Buffer controlled_buffer_11
  assign JumpCode = Bne_t ? 3'b001 : 3'bz;  // Controlled_Buffer controlled_buffer_12
  assign JumpCode = Blez_t ? 3'b010 : 3'bz;  // Controlled_Buffer controlled_buffer_13
  assign JumpCode = Bgtz_t ? 3'b011 : 3'bz;  // Controlled_Buffer controlled_buffer_14

  assign Destination = {Instruction[1:0], Instruction[15:8], Instruction[23:16], Instruction[31:24]};

  // Other names for the same wires on the sheet: Const[15:0] = Constante; Jump_t = Instruccion_J

  // Notes on the sheet:
  //   Instruccion tipo J
endmodule

// ID_R
module InstructionDecoder_R (
  input  [25:0] Input,
  output [3:0] Instruction,
  output [4:0] X,
  output [4:0] Rd,
  output [4:0] Rt,
  output [4:0] Rs,
  output [5:0] Func_code,
  output No_operacion,
  output Add,
  output Sub,
  output Mult,
  output Mulu,
  output Div,
  output Divu,
  output Slt,
  output Sltu,
  output And,
  output Or,
  output Nor,
  output XOr,
  output Push,
  output Jr,
  output Mfhi,
  output Mflo,
  output Pop
);

  wire xor_1_out, xor_2_out, xor_3_out;

  and and_1 (No_operacion, ~Input[0], ~Input[1], ~Input[2], ~Input[3], ~Input[4], ~Input[5]);  // AND_Gate
  and and_2 (Add, ~Input[0], ~Input[1], ~Input[2], ~Input[3], ~Input[4], Input[5]);  // AND_Gate
  and and_3 (Sub, ~Input[0], Input[1], ~Input[2], ~Input[3], ~Input[4], Input[5]);  // AND_Gate
  and and_4 (Mult, ~Input[0], ~Input[1], ~Input[2], Input[3], Input[4], ~Input[5]);  // AND_Gate
  and and_5 (Mulu, Input[0], ~Input[1], ~Input[2], Input[3], Input[4], ~Input[5]);  // AND_Gate
  and and_6 (Div, ~Input[0], Input[1], ~Input[2], Input[3], Input[4], ~Input[5]);  // AND_Gate
  and and_7 (Divu, Input[0], Input[1], ~Input[2], Input[3], Input[4], ~Input[5]);  // AND_Gate
  and and_8 (Slt, ~Input[0], Input[1], ~Input[2], Input[3], ~Input[4], Input[5]);  // AND_Gate
  and and_9 (Sltu, Input[0], Input[1], ~Input[2], Input[3], ~Input[4], Input[5]);  // AND_Gate
  and and_10 (And, ~Input[0], ~Input[1], Input[2], ~Input[3], ~Input[4], Input[5]);  // AND_Gate
  and and_11 (Or, Input[0], ~Input[1], Input[2], ~Input[3], ~Input[4], Input[5]);  // AND_Gate
  and and_12 (Nor, Input[0], Input[1], Input[2], ~Input[3], ~Input[4], Input[5]);  // AND_Gate
  and and_13 (XOr, ~Input[0], ~Input[1], ~Input[2], Input[3], ~Input[4], Input[5]);  // AND_Gate
  and and_14 (Push, Input[0], ~Input[1], ~Input[2], ~Input[3], ~Input[4], ~Input[5]);  // AND_Gate
  and and_15 (Jr, ~Input[0], ~Input[1], ~Input[2], Input[3], ~Input[4], ~Input[5]);  // AND_Gate
  and and_16 (Mfhi, ~Input[0], ~Input[1], ~Input[2], ~Input[3], Input[4], ~Input[5]);  // AND_Gate
  and and_17 (Mflo, ~Input[0], Input[1], ~Input[2], ~Input[3], Input[4], ~Input[5]);  // AND_Gate
  and and_18 (Pop, ~Input[0], ~Input[1], ~Input[2], ~Input[3], ~Input[4], ~Input[5]);  // AND_Gate
  xor xor_1 (xor_1_out, Mult, Mulu);
  xor xor_2 (xor_2_out, Div, Divu);
  xor xor_3 (xor_3_out, Slt, Sltu);
  assign Instruction = Add ? 4'b0000 : 4'bz;  // Controlled_Buffer controlled_buffer_1
  assign Instruction = Sub ? 4'b0001 : 4'bz;  // Controlled_Buffer controlled_buffer_2
  assign Instruction = xor_1_out ? 4'b0010 : 4'bz;  // Controlled_Buffer controlled_buffer_3
  assign Instruction = xor_2_out ? 4'b0011 : 4'bz;  // Controlled_Buffer controlled_buffer_4
  assign Instruction = xor_3_out ? 4'b0110 : 4'bz;  // Controlled_Buffer controlled_buffer_5
  assign Instruction = And ? 4'b1000 : 4'bz;  // Controlled_Buffer controlled_buffer_6
  assign Instruction = Or ? 4'b1010 : 4'bz;  // Controlled_Buffer controlled_buffer_7
  assign Instruction = Nor ? 4'b1011 : 4'bz;  // Controlled_Buffer controlled_buffer_8
  assign Instruction = XOr ? 4'b1100 : 4'bz;  // Controlled_Buffer controlled_buffer_9
  assign Instruction = No_operacion ? 4'b1111 : 4'bz;  // Controlled_Buffer controlled_buffer_10

  assign Func_code = Input[5:0];
  assign Rd = Input[15:11];
  assign Rs = Input[25:21];
  assign Rt = Input[20:16];
  assign X = Input[10:6];

  // Other names for the same wires on the sheet: No_Aritmetica = No_operacion

  // Notes on the sheet:
  //   Func-code
  //   X
  //   Rd
  //   Rt
  //   Rs
  //   Sub
  //   Mult
  //   Div
  //   Divu
  //   Slt
  //   Sltu
  //   And
  //   Or
  //   Nor
  //   XOr
  //   Push
  //   Jr
  //   Mfhi
  //   MfLo
  //   Push
  //   Add
  //   Mulu
endmodule

// ID_J
module InstructionDecoder_J (
  input  [31:0] Instruction,
  input  [3:0] PC,
  output [31:0] PC_2
);


  assign PC_2 = {PC, Instruction[25:0], 2'b00};
endmodule

// ID_I
module InstructionDecoder_I (
  input  [25:0] Instruction,
  input  [5:0] Operacion,
  output [15:0] Constante,
  output [4:0] Rt,
  output [4:0] Rs,
  output Addi,
  output Slti,
  output Sltiu,
  output Andi,
  output Ori,
  output XOri,
  output Lw,
  output Sw,
  output Beq,
  output Bne,
  output Blez,
  output Bgtz,
  output Bltz,
  output [3:0] Instruction_2
);

  wire or_1_out;

  and and_1 (Addi, ~Operacion[0], ~Operacion[1], ~Operacion[2], Operacion[3], ~Operacion[4], ~Operacion[5]);  // AND_Gate
  and and_2 (Slti, ~Operacion[0], Operacion[1], ~Operacion[2], Operacion[3], ~Operacion[4], ~Operacion[5]);  // AND_Gate
  and and_3 (Sltiu, Operacion[0], Operacion[1], ~Operacion[2], Operacion[3], ~Operacion[4], ~Operacion[5]);  // AND_Gate
  and and_4 (Andi, ~Operacion[0], ~Operacion[1], Operacion[2], Operacion[3], ~Operacion[4], ~Operacion[5]);  // AND_Gate
  and and_5 (Ori, Operacion[0], ~Operacion[1], Operacion[2], Operacion[3], ~Operacion[4], ~Operacion[5]);  // AND_Gate
  and and_6 (XOri, ~Operacion[0], Operacion[1], Operacion[2], Operacion[3], ~Operacion[4], ~Operacion[5]);  // AND_Gate
  and and_7 (Lw, Operacion[0], Operacion[1], ~Operacion[2], ~Operacion[3], ~Operacion[4], Operacion[5]);  // AND_Gate
  and and_8 (Sw, Operacion[0], Operacion[1], ~Operacion[2], Operacion[3], ~Operacion[4], Operacion[5]);  // AND_Gate
  and and_9 (Beq, ~Operacion[0], ~Operacion[1], Operacion[2], ~Operacion[3], ~Operacion[4], ~Operacion[5]);  // AND_Gate
  and and_10 (Bne, Operacion[0], ~Operacion[1], Operacion[2], ~Operacion[3], ~Operacion[4], ~Operacion[5]);  // AND_Gate
  and and_11 (Blez, ~Operacion[0], Operacion[1], Operacion[2], ~Operacion[3], ~Operacion[4], ~Operacion[5]);  // AND_Gate
  and and_12 (Bgtz, Operacion[0], Operacion[1], Operacion[2], ~Operacion[3], ~Operacion[4], ~Operacion[5]);  // AND_Gate
  and and_13 (Bltz, Operacion[0], ~Operacion[1], ~Operacion[2], ~Operacion[3], ~Operacion[4], ~Operacion[5]);  // AND_Gate
  or or_1 (or_1_out, Slti, Sltiu);
  assign Instruction_2 = Addi ? 4'b0000 : 4'bz;  // Controlled_Buffer controlled_buffer_1
  assign Instruction_2 = or_1_out ? 4'b0110 : 4'bz;  // Controlled_Buffer controlled_buffer_2
  assign Instruction_2 = Andi ? 4'b1000 : 4'bz;  // Controlled_Buffer controlled_buffer_3
  assign Instruction_2 = Ori ? 4'b1010 : 4'bz;  // Controlled_Buffer controlled_buffer_4
  assign Instruction_2 = XOri ? 4'b1100 : 4'bz;  // Controlled_Buffer controlled_buffer_5

  assign Constante = Instruction[15:0];
  assign Rs = Instruction[25:21];
  assign Rt = Instruction[20:16];

  // Other names for the same wires on the sheet: Const[15:0] = Instruction[15:0]; Op[5:0] = Operacion

  // Notes on the sheet:
  //   Addi
  //   Slti
  //   Sltiu
  //   Andi
  //   Ori
  //   XOri
  //   Lw
  //   Sw
  //   Beq
  //   Bne
  //   Blez
  //   Bgtz
  //   Bltz
endmodule

// ID_R_E
module InstructionDecoder_R_Especial (
  input  [5:0] Func_code,
  output Halt,
  output Tty,
  output Rnd,
  output Kbd
);

  and and_1 (Halt, Func_code[0], Func_code[1], Func_code[2], Func_code[3], Func_code[4], Func_code[5]);
  and and_2 (Tty, Func_code[0], ~Func_code[1], ~Func_code[2], ~Func_code[3], ~Func_code[4], ~Func_code[5]);  // AND_Gate
  and and_3 (Rnd, ~Func_code[0], Func_code[1], ~Func_code[2], ~Func_code[3], ~Func_code[4], ~Func_code[5]);  // AND_Gate
  and and_4 (Kbd, ~Func_code[0], ~Func_code[1], Func_code[2], ~Func_code[3], ~Func_code[4], ~Func_code[5]);  // AND_Gate

  // Notes on the sheet:
  //   Halt
  //   Tty
  //   Rnd
  //   Kbd
endmodule

module BranchControl (
  input  [2:0] in_1,
  input  [31:0] RS,
  input  [31:0] RT,
  input  [31:0] in_4,
  input  [15:0] OFSSET,
  input  [25:0] Destination,
  output [31:0] Salida
);

  wire [31:0] BeqResoult, BgtzResoult, BlezResoult, BltzResoult, BneResoult, JumpRegisterResoult, JumpResoult;

  Beq beq_1 (.in_1(RS), .in_2(RT), .in_3(in_4), .in_4(OFSSET), .Output(BeqResoult));
  Bne bne_1 (.in_1(RS), .in_2(RT), .in_3(in_4), .in_4(OFSSET), .Output(BneResoult));
  Blez blez_1 (.in_1(RS), .in_2(in_4), .in_3(OFSSET), .Output(BlezResoult));
  Bgtz bgtz_1 (.in_1(RS), .in_2(in_4), .in_3(OFSSET), .Output(BgtzResoult));
  Bltz bltz_1 (.in_1(RS), .in_2(in_4), .in_3(OFSSET), .Output(BltzResoult));
  Jump jump_1 (.in_1(Destination), .in_2(in_4), .out_3(JumpResoult));
  JumpRegister jumpregister_1 (.in_1(RS), .JumpRegister(JumpRegisterResoult));
  Multiplexer #(.select(3), .width(32)) multiplexer_1 (
    .in0(BeqResoult), .in1(BneResoult), .in2(BlezResoult), .in3(BgtzResoult), .in4(BltzResoult),
    .in5(JumpResoult), .in6(JumpRegisterResoult), .out(Salida), .sel(in_1));  // open: in7, en

  // Other names for the same wires on the sheet: OFFSET[15:0] = OFSSET; PC[31:0] = in_4; Selector[2:0] = in_1

  // Notes on the sheet:
  //   PC
  //   OFFSET
  //   Destination
  //   RS
  //   RT
  //   Beq
  //   Bne
  //   Blez
  //   Bgtz
  //   Bltz
  //   Jump
  //   JumpRegister
  //   BranchControlUnit
endmodule

module Beq (
  input  [31:0] in_1,
  input  [31:0] in_2,
  input  [31:0] in_3,
  input  [15:0] in_4,
  output [31:0] Output
);

  wire comparator_1_eq, not_1_out;
  wire [31:0] adder_1_out;

  Comparator #(.width(32), .mode("unsigned")) comparator_1 (.a(in_1), .b(in_2), .eq(comparator_1_eq));  // open: gt, lt
  not not_1 (not_1_out, comparator_1_eq);
  assign Output = not_1_out ? in_3 : 32'bz;  // Controlled_Buffer controlled_buffer_1
  assign Output = comparator_1_eq ? adder_1_out : 32'bz;  // Controlled_Buffer controlled_buffer_2
  Adder #(.width(32)) adder_1 (
    .a(in_3), .b({{15{in_4[15]}}, in_4[14:0], 2'b00}), .out(adder_1_out));  // open: cin, cout

  // Other names for the same wires on the sheet: PC[31:0] = in_3; RS[31:0] = in_1; RT[31:0] = in_2

  // Notes on the sheet:
  //   PC
  //   OFFSET
  //   RS
  //   RT
  //   BEQ
endmodule

module Bne (
  input  [31:0] in_1,
  input  [31:0] in_2,
  input  [31:0] in_3,
  input  [15:0] in_4,
  output [31:0] Output
);

  wire comparator_1_eq, not_1_out, not_2_out;
  wire [31:0] adder_1_out;

  not not_1 (not_1_out, comparator_1_eq);
  Comparator #(.width(32)) comparator_1 (.a(in_1), .b(in_2), .eq(comparator_1_eq));  // open: gt, lt
  not not_2 (not_2_out, not_1_out);
  assign Output = not_2_out ? in_3 : 32'bz;  // Controlled_Buffer controlled_buffer_1
  Adder #(.width(32)) adder_1 (
    .a(in_3), .b({{15{in_4[15]}}, in_4[14:0], 2'b00}), .out(adder_1_out));  // open: cin, cout
  assign Output = not_1_out ? adder_1_out : 32'bz;  // Controlled_Buffer controlled_buffer_2

  // Other names for the same wires on the sheet: PC[31:0] = in_3; RS[31:0] = in_1; RT[31:0] = in_2

  // Notes on the sheet:
  //   OFFSET
  //   RS
  //   RT
  //   PC
  //   BNE
endmodule

module Blez (
  input  [31:0] in_1,
  input  [31:0] in_2,
  input  [15:0] in_3,
  output [31:0] Output
);

  wire comparator_1_eq, comparator_1_lt, not_1_out, or_1_out;
  wire [31:0] adder_1_out;

  Comparator #(.width(32)) comparator_1 (
    .a(in_1), .b({32{1'b0}}), .eq(comparator_1_eq), .lt(comparator_1_lt));  // open: gt
  or or_1 (or_1_out, comparator_1_eq, comparator_1_lt);
  not not_1 (not_1_out, or_1_out);
  assign Output = not_1_out ? in_2 : 32'bz;  // Controlled_Buffer controlled_buffer_1
  Adder #(.width(32)) adder_1 (
    .a(in_2), .b({{15{in_3[15]}}, in_3[14:0], 2'b00}), .out(adder_1_out));  // open: cin, cout
  assign Output = or_1_out ? adder_1_out : 32'bz;  // Controlled_Buffer controlled_buffer_2

  // Other names for the same wires on the sheet: PC[31:0] = in_2; RS[31:0] = in_1

  // Notes on the sheet:
  //   OFFSET
  //   RS
  //   PC
  //   BLEZ
endmodule

module Bgtz (
  input  [31:0] in_1,
  input  [31:0] in_2,
  input  [15:0] in_3,
  output [31:0] Output
);

  wire comparator_1_gt, not_1_out;
  wire [31:0] adder_1_out;

  Comparator #(.width(32)) comparator_1 (.a(in_1), .b({32{1'b0}}), .gt(comparator_1_gt));  // open: eq, lt
  not not_1 (not_1_out, comparator_1_gt);
  assign Output = not_1_out ? in_2 : 32'bz;  // Controlled_Buffer controlled_buffer_1
  Adder #(.width(32)) adder_1 (
    .a(in_2), .b({{15{in_3[15]}}, in_3[14:0], 2'b00}), .out(adder_1_out));  // open: cin, cout
  assign Output = comparator_1_gt ? adder_1_out : 32'bz;  // Controlled_Buffer controlled_buffer_2

  // Other names for the same wires on the sheet: PC[31:0] = in_2; RS[31:0] = in_1

  // Notes on the sheet:
  //   OFFSET
  //   RS
  //   PC
  //   BGTZ
endmodule

module Bltz (
  input  [31:0] in_1,
  input  [31:0] in_2,
  input  [15:0] in_3,
  output [31:0] Output
);

  wire comparator_1_lt, not_1_out;
  wire [31:0] adder_1_out;

  Comparator #(.width(32)) comparator_1 (.a(in_1), .b({32{1'b0}}), .lt(comparator_1_lt));  // open: gt, eq
  not not_1 (not_1_out, comparator_1_lt);
  assign Output = not_1_out ? in_2 : 32'bz;  // Controlled_Buffer controlled_buffer_1
  Adder #(.width(32)) adder_1 (
    .a(in_2), .b({{15{in_3[15]}}, in_3[14:0], 2'b00}), .out(adder_1_out));  // open: cin, cout
  assign Output = comparator_1_lt ? adder_1_out : 32'bz;  // Controlled_Buffer controlled_buffer_2

  // Other names for the same wires on the sheet: PC[31:0] = in_2; RS[31:0] = in_1

  // Notes on the sheet:
  //   OFFSET
  //   RS
  //   PC
  //   BLTZ
endmodule

module Jump (
  input  [25:0] in_1,
  input  [31:0] in_2,
  output [31:0] out_3
);

  Subtractor #(.width(32)) subtractor_1 (.a({in_2[31:28], in_1, 2'b00}), .b(32'h4), .out(out_3));  // open: bin, bout

  // Notes on the sheet:
  //   Destination
  //   PC
  //   JUMP
endmodule

module JumpRegister (
  input  [31:0] in_1,
  output [31:0] JumpRegister
);

  Subtractor #(.width(32)) subtractor_1 (.a(in_1), .b(32'h4), .out(JumpRegister));  // open: bin, bout

  // Notes on the sheet:
  //   RS
  //   JumpRegister
endmodule

module rnd (
  input  in_1,
  output [31:0] Output
);

  wire clock_1_out;

  Clock clock_1 (.out(clock_1_out));
  Random #(.width(32)) random_1 (.clk(clock_1_out), .next(in_1), .out(Output));  // open: clr

  // Notes on the sheet:
  //   RND
endmodule

module Control_Unity (
  input  [31:0] Input_Ram_0,
  input  [31:0] Input_Ram_1,
  input  [31:0] Input_Ram_2,
  input  [31:0] Input_Ram_3,
  input  [15:0] Block,
  output [3:0] Mask,
  output [31:0] Data_from_Ram
);

  Multiplexer #(.select(2), .width(32)) multiplexer_1 (
    .in0(Input_Ram_0), .in1(Input_Ram_1), .in2(Input_Ram_2), .in3(Input_Ram_3), .out(Data_from_Ram),
    .sel(Block[1:0]));  // open: en
  and and_1 (Mask[0], ~Block[0], ~Block[1]);  // AND_Gate
  and and_2 (Mask[1], Block[0], ~Block[1]);  // AND_Gate
  and and_3 (Mask[2], ~Block[0], Block[1]);  // AND_Gate
  and and_4 (Mask[3], Block[1], Block[0]);

  // Other names for the same wires on the sheet: Bloque[1:0] = Block[1:0]

  // Notes on the sheet:
  //   Mask
  //   Bank 0
  //   Bank 1
  //   Bank 2
  //   Bank 3
endmodule

module LS_SW_PUSH (
  input  [15:0] OFFSET,
  input  [31:0] in_2,
  input  [31:0] in_3,
  input  PUSH,
  input  SW,
  output [31:0] RAMInput0,
  output [31:0] RAMAddress
);

  wire [1:0] Dir;
  wire [31:0] multiplexer_1_out, multiplexer_2_out;

  Adder #(.width(32)) adder_1 (
    .a({{17{OFFSET[15]}}, OFFSET[14:0]}), .b(in_2), .out({RAMAddress[31:2], Dir}));  // open: cin, cout
  Multiplexer #(.width(32)) multiplexer_1 (
    .in0({32{1'b0}}), .in1(in_2), .out(multiplexer_1_out), .sel(PUSH));  // open: en
  Multiplexer #(.width(32)) multiplexer_2 (
    .in0({32{1'b0}}), .in1(in_3), .out(multiplexer_2_out), .sel(SW));  // open: en
  Multiplexer #(.width(32)) multiplexer_3 (
    .in0(multiplexer_1_out), .in1(multiplexer_2_out), .out(RAMInput0), .sel(SW));  // open: en

  assign RAMAddress[1:0] = 2'b00;

  // Other names for the same wires on the sheet: Dir[31:2] = RAMAddress[31:2]; RS[31:0] = in_2; RT[31:0] = in_3

  // Notes on the sheet:
  //   LW/SW
  //   Ram Dir
endmodule

module SP_Address (
  input  SPpop,
  input  [4:0] SPContent,
  input  Push,
  output [4:0] SPNewContent
);

  wire [4:0] adder_1_out, controlled_buffer_1_out, subtractor_1_out;

  Adder #(.width(5)) adder_1 (.a(SPContent), .b(5'b00001), .out(adder_1_out));  // open: cin, cout
  Subtractor #(.width(5)) subtractor_1 (.a(SPContent), .b(5'b00001), .out(subtractor_1_out));  // open: bin, bout
  assign controlled_buffer_1_out = SPpop ? adder_1_out : 5'bz;  // Controlled_Buffer controlled_buffer_1
  Multiplexer #(.width(5)) multiplexer_1 (
    .in0(controlled_buffer_1_out), .in1(subtractor_1_out), .out(SPNewContent), .sel(Push));  // open: en

  // Notes on the sheet:
  //   Push/Pop
endmodule

module PC (
  input  GetJump,
  input  Next,
  input  CLR,
  input  RRam,
  input  Rw,
  input  [31:0] Jump,
  input  [31:0] SP,
  input  [31:0] Ram_Addres,
  input  LW,
  input  SW,
  output [15:0] Block,
  output [15:0] RAM_A,
  output [31:0] PC
);

  wire clock_1_out, or_1_out, or_2_out, or_3_out;
  wire [31:0] adder_1_out, multiplexer_1_out, multiplexer_2_out, multiplexer_3_out, multiplexer_4_out;

  Multiplexer #(.width(32)) multiplexer_1 (
    .in0({32{1'b0}}), .in1(32'h4), .out(multiplexer_1_out), .sel(Next));  // open: en
  Adder #(.width(32)) adder_1 (.a(PC), .b(multiplexer_1_out), .out(adder_1_out));  // open: cin, cout
  Multiplexer #(.width(32)) multiplexer_2 (
    .in0(SP), .in1(Ram_Addres), .out(multiplexer_2_out), .sel(or_1_out));  // open: en
  or or_1 (or_1_out, LW, SW);
  Multiplexer #(.width(32)) multiplexer_3 (
    .in0(adder_1_out), .in1(Jump), .out(multiplexer_3_out), .sel(GetJump));  // open: en
  Clock clock_1 (.out(clock_1_out));
  or or_2 (or_2_out, GetJump, Next);
  // Probe on PC
  Register #(.width(32)) register_1 (.D(multiplexer_3_out), .en(or_2_out), .Q(PC), .clk(clock_1_out), .clr(CLR));
  Multiplexer #(.width(32)) multiplexer_4 (
    .in0(PC), .in1(multiplexer_2_out),
    .out({multiplexer_4_out[31:18], RAM_A[13:0], Block[1:0], multiplexer_4_out[1:0]}), .sel(or_3_out));  // open: en
  or or_3 (or_3_out, Rw, RRam);

  assign Block[15:2] = {14{1'b0}};
  assign RAM_A[15:14] = 2'b00;

  // Notes on the sheet:
  //   ProgramCounter
endmodule

module Reading_Writing_Ram (
  input  [3:0] Read_Time,
  input  Read_Ram_1,
  input  Write_Ram,
  input  Read_Ram_2,
  input  [3:0] Write_Time,
  output Ready,
  output Finished
);

  wire clock_1_out, clock_2_out, comparator_2_gt, comparator_4_gt, or_1_out, or_2_out;
  wire [3:0] counter_1_q, counter_2_q;

  Counter #(.width(4), .max('hf)) counter_1 (
    .D(counter_1_q), .Q(counter_1_q), .clk(clock_1_out), .clr(or_1_out));  // open: load, count, carry
  Clock clock_1 (.out(clock_1_out));
  // Probe on counter_1_q
  or or_1 (or_1_out, comparator_2_gt, Read_Ram_1, Read_Ram_2);
  Comparator #(.width(4)) comparator_1 (.a(counter_1_q), .b(Read_Time), .eq(Ready));  // open: gt, lt
  Comparator #(.width(4)) comparator_2 (.a(counter_1_q), .b(Read_Time), .gt(comparator_2_gt));  // open: eq, lt
  Counter #(.width(4), .max('hf)) counter_2 (
    .D(counter_2_q), .Q(counter_2_q), .clk(clock_2_out), .clr(or_2_out));  // open: load, count, carry
  Clock clock_2 (.out(clock_2_out));
  Comparator #(.width(4), .mode("unsigned")) comparator_3 (
    .a(counter_2_q), .b(Write_Time), .eq(Finished));  // open: gt, lt
  or or_2 (or_2_out, comparator_4_gt, Write_Ram);
  Comparator #(.width(4), .mode("unsigned")) comparator_4 (
    .a(counter_2_q), .b(Write_Time), .gt(comparator_4_gt));  // open: eq, lt

  // Notes on the sheet:
  //   Reading Ram
  //   Writing Ram
endmodule

module DATA_INPUT (
  input  [31:0] RAM_OUTPUT_0,
  input  Pop1,
  input  CLR,
  input  [31:0] KbdData,
  input  Lw1,
  input  sltiu_slti,
  input  [31:0] ResoultAlu,
  input  rnd,
  input  Kbd,
  input  Push,
  input  [31:0] Lo_Output,
  input  [31:0] Hi_Output,
  input  Mflo,
  input  Mfhi,
  input  [31:0] Slti_Sltiu,
  input  [31:0] rnd_2,
  output [31:0] DATA_OUTPUT
);

  wire and_1_out, clock_1_out, or_1_out, or_2_out;
  wire [31:0] multiplexer_1_out, multiplexer_2_out, multiplexer_3_out, multiplexer_4_out, multiplexer_5_out,
       register_1_q;

  Register #(.width(32)) register_1 (.D(RAM_OUTPUT_0), .en(or_2_out), .Q(register_1_q), .clk(clock_1_out), .clr(CLR));
  Clock clock_1 (.out(clock_1_out));
  Multiplexer #(.width(32)) multiplexer_1 (
    .in0(Lo_Output), .in1(Hi_Output), .out(multiplexer_1_out), .sel(and_1_out));  // open: en
  and and_1 (and_1_out, ~Mflo, Mfhi);  // AND_Gate
  Multiplexer #(.width(32)) multiplexer_2 (
    .in0(ResoultAlu), .in1(multiplexer_1_out), .out(multiplexer_2_out), .sel(or_1_out));  // open: en
  or or_1 (or_1_out, Mflo, Mfhi);
  or or_2 (or_2_out, Lw1, Pop1, Push);
  Multiplexer #(.width(32)) multiplexer_3 (
    .in0(multiplexer_2_out), .in1(register_1_q), .out(multiplexer_3_out), .sel(or_2_out));  // open: en
  Multiplexer #(.width(32)) multiplexer_4 (
    .in0(multiplexer_3_out), .in1(Slti_Sltiu), .out(multiplexer_4_out), .sel(sltiu_slti));  // open: en
  Multiplexer #(.width(32)) multiplexer_5 (
    .in0(multiplexer_4_out), .in1(rnd_2), .out(multiplexer_5_out), .sel(rnd));  // open: en
  Multiplexer #(.width(32)) multiplexer_6 (
    .in0(multiplexer_5_out), .in1(KbdData), .out(DATA_OUTPUT), .sel(Kbd));  // open: en
endmodule

// CLR
module DATA_ADDRESS (
  input  Lw,
  input  Pop,
  input  CLR,
  input  [4:0] Rt,
  input  [4:0] Rd,
  input  RD_2,
  input  rnd,
  input  Pop1,
  input  Lw1,
  output [4:0] Output_ADDRESS
);

  wire clock_1_out, nor_1_out, or_1_out, or_2_out;
  wire [4:0] multiplexer_1_out, register_1_q;

  or or_1 (or_1_out, RD_2, Pop, rnd);
  Multiplexer #(.width(5)) multiplexer_1 (.in0(Rt), .in1(Rd), .out(multiplexer_1_out), .sel(or_1_out));  // open: en
  Register #(.width(5)) register_1 (
    .D(multiplexer_1_out), .en(or_2_out), .Q(register_1_q), .clk(clock_1_out), .clr(CLR));
  or or_2 (or_2_out, Lw, Pop);
  Clock clock_1 (.out(clock_1_out));
  nor nor_1 (nor_1_out, Pop1, Lw1);
  Multiplexer #(.width(5)) multiplexer_2 (
    .in0(register_1_q), .in1(multiplexer_1_out), .out(Output_ADDRESS), .sel(nor_1_out));  // open: en
endmodule

module DATA_PATH (
  input  Kbd,
  input  Add,
  input  Sub,
  input  Slt,
  input  Sltu,
  input  Pop,
  input  And,
  input  Mflo,
  input  Push,
  input  Sw,
  input  Nor,
  input  Xor,
  input  Mfhi,
  input  Addi,
  input  Slti,
  input  Sltiu,
  input  Or,
  input  Finished,
  input  Andi,
  input  Ori,
  input  Xori,
  input  Beq,
  input  Bne,
  input  Blez,
  input  Bgtz,
  input  Bltz,
  input  Jump,
  input  Lw,
  input  Jr,
  input  Nop,
  input  Ready,
  input  CLR,
  input  rnd,
  input  Halt,
  input  Tty,
  output Write_Ram,
  output RW,
  output KBD_CLR,
  output RRam,
  output Read_Ram_1,
  output GetJump,
  output Get_Instruction,
  output RF_E,
  output Read_Ram_2,
  output Kbd_Enable,
  output TTY_ENABLE,
  output Next,
  output Pop1,
  output SPpop,
  output Lw1,
  output SPEnable
);

  wire and_1_out, and_2_out, CLK, clock_2_out, clock_3_out, demultiplexer_1_out0, demultiplexer_2_out0,
       demultiplexer_3_out0, demultiplexer_3_out1, demultiplexer_4_out0, demultiplexer_4_out1,
       demultiplexer_5_out0, demultiplexer_5_out1, demultiplexer_6_out0, demultiplexer_7_out0,
       demultiplexer_7_out1, demultiplexer_8_out0, demultiplexer_9_out0, demultiplexer_9_out1,
       demultiplexer_10_out0, demultiplexer_10_out1, demultiplexer_11_out0, demultiplexer_11_out1,
       demultiplexer_12_out1, demultiplexer_13_out0, demultiplexer_14_out0, demultiplexer_15_out0,
       demultiplexer_15_out1, demultiplexer_16_out0, demultiplexer_16_out1, demultiplexer_17_out0, END_q,
       EndLW, FinishedRF, IDLE_q, Jumping, NextPop, or_1_out, or_3_out, or_5_out, or_7_out, or_8_out,
       or_9_out, or_10_out, or_11_out, or_12_out, or_13_out, or_14_out, or_15_out, or_20_out, or_23_out,
       or_25_out, or_26_out, or_27_out, RF1, RF2, RF4, RF_Enable1, RF_Enable2, RF_Enable3, rnd_q, SPpush,
       StartLw, trigger, triggerRND, undriven, Write_Ram_q, Write_RF_q, WriteRF_2_q, WriteRF_3_q,
       WriteRF_4_q, WriteRF_q, WritingTask;

  D_Flip_Flop IDLE (.clk(CLK), .D(or_1_out), .Q(IDLE_q), .preset(and_1_out));  // open: Qn, en, reset
  or or_1 (or_1_out, demultiplexer_1_out0, Next);
  and and_1 (and_1_out, CLR, ~END_q);  // AND_Gate
  or or_2 (Jumping, Beq, Bne, Blez, Bgtz, Bltz, Jump, Jr);
  Demultiplexer demultiplexer_1 (.out0(demultiplexer_1_out0), .out1(KBD_CLR), .in(IDLE_q), .sel(1'b1));  // open: en
  or or_3 (or_3_out, Add, Sub, Slt, Sltu, And, Nor, Xor, Addi, Slti, Sltiu, Or, Andi, Ori, Xori);
  Clock clock_1 (.out(CLK));
  or or_4 (Next, demultiplexer_2_out0, TTY_ENABLE);
  or or_5 (or_5_out, demultiplexer_3_out0, KBD_CLR);
  or or_6 (WritingTask, Kbd, Pop, rnd, Mflo, or_3_out, Jumping, Mfhi, Pop1);
  and and_2 (and_2_out, or_5_out, ~Ready);  // AND_Gate
  Demultiplexer demultiplexer_2 (
    .out0(demultiplexer_2_out0), .out1(TTY_ENABLE), .in(demultiplexer_4_out1), .sel(Tty));  // open: en
  D_Flip_Flop u_Get_Instruction (.clk(CLK), .D(and_2_out), .Q(Get_Instruction), .reset(CLR));  // open: Qn, preset, en
  or or_7 (or_7_out, demultiplexer_4_out0, or_9_out);
  Demultiplexer demultiplexer_3 (
    .out0(demultiplexer_3_out0), .out1(demultiplexer_3_out1), .in(Get_Instruction), .sel(Ready));  // open: en
  D_Flip_Flop END (.clk(CLK), .D(or_7_out), .Q(END_q), .reset(CLR));  // open: Qn, preset, en
  Demultiplexer demultiplexer_4 (
    .out0(demultiplexer_4_out0), .out1(demultiplexer_4_out1), .in(END_q), .sel(or_8_out));  // open: en
  or or_8 (or_8_out, CLR, ~Halt);  // OR_Gate
  D_Flip_Flop InstructionReady (.clk(CLK), .D(demultiplexer_3_out1), .Q(NextPop), .reset(CLR));  // open: Qn, preset, en
  or or_9 (or_9_out, demultiplexer_5_out1, or_13_out);
  Demultiplexer demultiplexer_5 (
    .out0(demultiplexer_5_out0), .out1(demultiplexer_5_out1), .in(NextPop), .sel(Nop), .en(undriven));
  Register #(.width(1)) register_1 (.D(StartLw), .en(StartLw), .Q(Lw1), .clk(CLK), .clr(EndLW));
  Demultiplexer demultiplexer_6 (
    .out0(demultiplexer_6_out0), .out1(Read_Ram_1), .in(demultiplexer_5_out0), .sel(or_10_out));  // open: en
  or or_10 (or_10_out, Lw, Pop);
  and and_3 (Kbd_Enable, Kbd, or_13_out);
  Register #(.width(1)) register_2 (.D(Pop), .en(Pop), .Q(Pop1), .clk(CLK), .clr(NextPop));
  or or_11 (or_11_out, Push, Sw);
  Demultiplexer demultiplexer_7 (
    .out0(demultiplexer_7_out0), .out1(demultiplexer_7_out1), .in(demultiplexer_6_out0), .sel(or_11_out));  // open: en
  Demultiplexer demultiplexer_8 (
    .out0(demultiplexer_8_out0), .out1(RF1), .in(demultiplexer_7_out1), .sel(Push));  // open: en
  or or_12 (or_12_out, demultiplexer_9_out0, Read_Ram_1);
  or or_13 (or_13_out, demultiplexer_13_out0, demultiplexer_10_out1);
  Clock clock_2 (.out(clock_2_out));
  or or_14 (or_14_out, RF2, RF1, RF4);
  D_Flip_Flop readRAM (.clk(CLK), .D(or_12_out), .Q(RRam), .reset(CLR));  // open: Qn, preset, en
  D_Flip_Flop #(.trigger("falling")) d_ff_1 (
    .clk(clock_2_out), .D(1'b1), .Q(FinishedRF), .reset(or_14_out));  // open: Qn, preset, en
  or or_15 (or_15_out, demultiplexer_11_out0, RF1);
  and and_4 (StartLw, Lw, RRam);
  Demultiplexer demultiplexer_9 (
    .out0(demultiplexer_9_out0), .out1(demultiplexer_9_out1), .in(RRam), .sel(Ready));  // open: en
  D_Flip_Flop d_ff_2 (.clk(CLK), .D(or_15_out), .Q(SPpush), .reset(CLR));  // open: Qn, preset, en
  and and_5 (GetJump, Jumping, Write_RF_q);
  D_Flip_Flop Write_RF (.clk(CLK), .D(RF_Enable2), .Q(Write_RF_q), .reset(CLR));  // open: Qn, preset, en
  Demultiplexer demultiplexer_10 (
    .out0(demultiplexer_10_out0), .out1(demultiplexer_10_out1), .in(Write_RF_q), .sel(FinishedRF));  // open: en
  and and_6 (SPpop, Pop1, RF_Enable2);
  or or_16 (SPEnable, SPpop, SPpush);
  Demultiplexer demultiplexer_11 (
    .out0(demultiplexer_11_out0), .out1(demultiplexer_11_out1), .in(SPpush), .sel(FinishedRF));  // open: en
  D_Flip_Flop WriteRF (.clk(CLK), .D(demultiplexer_9_out1), .Q(WriteRF_q), .reset(CLR));  // open: Qn, preset, en
  or or_17 (RF_Enable2, demultiplexer_10_out0, RF2);
  Clock clock_3 (.out(clock_3_out));
  Demultiplexer demultiplexer_12 (.out0(RF4), .out1(demultiplexer_12_out1), .in(WriteRF_q), .sel(Pop1));  // open: en
  or or_18 (RF_E, RF_Enable2, RF_Enable3, RF_Enable1);
  D_Flip_Flop #(.trigger("high")) d_ff_3 (
    .clk(clock_3_out), .D(1'b1), .Q(triggerRND), .reset(trigger));  // open: Qn, preset, en
  or or_19 (Write_Ram, demultiplexer_8_out0, demultiplexer_11_out1);
  or or_20 (or_20_out, demultiplexer_14_out0, RF4);
  Demultiplexer demultiplexer_13 (
    .out0(demultiplexer_13_out0), .out1(RF2), .in(or_23_out), .sel(WritingTask));  // open: en
  or or_21 (RW, demultiplexer_15_out0, Write_Ram);
  or or_22 (RF_Enable1, RF4, or_20_out, WriteRF_2_q);
  D_Flip_Flop WriteRF_2 (.clk(CLK), .D(or_20_out), .Q(WriteRF_2_q), .reset(CLR));  // open: Qn, preset, en
  or or_23 (or_23_out, demultiplexer_17_out0, demultiplexer_16_out1);
  Demultiplexer demultiplexer_14 (
    .out0(demultiplexer_14_out0), .out1(EndLW), .in(WriteRF_2_q), .sel(FinishedRF));  // open: en
  D_Flip_Flop u_Write_Ram (.clk(CLK), .D(RW), .Q(Write_Ram_q), .reset(CLR));  // open: Qn, preset, en
  D_Flip_Flop WriteRF_3 (.clk(CLK), .D(demultiplexer_12_out1), .Q(WriteRF_3_q), .reset(CLR));  // open: Qn, preset, en
  D_Flip_Flop u_rnd (.clk(CLK), .D(or_25_out), .Q(rnd_q), .reset(CLR));  // open: Qn, preset, en
  Demultiplexer demultiplexer_15 (
    .out0(demultiplexer_15_out0), .out1(demultiplexer_15_out1), .in(Write_Ram_q), .sel(Finished));  // open: en
  D_Flip_Flop WriteRF_4 (.clk(CLK), .D(WriteRF_3_q), .Q(WriteRF_4_q));  // open: Qn, preset, en, reset
  or or_24 (RF_Enable3, demultiplexer_12_out1, WriteRF_3_q, WriteRF_4_q);
  Demultiplexer demultiplexer_16 (
    .out0(demultiplexer_16_out0), .out1(demultiplexer_16_out1), .in(rnd_q), .sel(triggerRND));  // open: en
  or or_25 (or_25_out, demultiplexer_16_out0, trigger);
  or or_26 (or_26_out, demultiplexer_7_out0, demultiplexer_15_out1);
  or or_27 (or_27_out, or_26_out, EndLW, WriteRF_4_q);
  Demultiplexer demultiplexer_17 (.out0(demultiplexer_17_out0), .out1(trigger), .in(or_27_out), .sel(rnd));  // open: en

  assign Read_Ram_2 = KBD_CLR;

  // Notes on the sheet:
  //   Data_Path
endmodule

module Utilities (
  input  [15:0] Offset,
  input  [31:0] RT,
  input  Mflo,
  input  Add,
  input  Sub,
  input  Mult,
  input  Mulu,
  input  Div,
  input  Divu,
  input  Slt,
  input  Sltu,
  input  And,
  input  Xor,
  input  Nor,
  input  Mfhi,
  input  OR,
  input  Kbd,
  output [31:0] A,
  output RD
);

  or or_1 (RD, Mflo, Add, Sub, Mult, Mulu, Div, Divu, Slt, Sltu, And, Xor, Nor, Mfhi, OR, Kbd);
  Multiplexer #(.width(32)) multiplexer_1 (
    .in0({{17{Offset[15]}}, Offset[14:0]}), .in1(RT), .out(A), .sel(RD));  // open: en
endmodule

module Useful (
  input  Trigger,
  input  [15:0] Offset,
  input  [31:0] RS,
  input  sltiu,
  output [31:0] Rd,
  output [31:0] Rt
);

  wire comparator_1_gt;
  wire [15:0] multiplexer_1_out;
  wire [31:0] multiplexer_2_out;

  rnd rnd_1 (.in_1(Trigger), .Output(Rd));
  Multiplexer #(.width(16)) multiplexer_1 (
    .in0(Offset), .in1({1'b0, Offset[14:0]}), .out(multiplexer_1_out), .sel(sltiu));  // open: en
  Multiplexer #(.width(32)) multiplexer_2 (
    .in0(RS), .in1({1'b0, RS[30:0]}), .out(multiplexer_2_out), .sel(sltiu));  // open: en
  Comparator #(.width(32)) comparator_1 (
    .a({{17{multiplexer_1_out[15]}}, multiplexer_1_out[14:0]}), .b(multiplexer_2_out), .gt(comparator_1_gt));  // open: eq, lt
  Multiplexer #(.width(32)) multiplexer_3 (.in0({32{1'b0}}), .in1(32'h1), .out(Rt), .sel(comparator_1_gt));  // open: en
endmodule

module KBD (
  input  [6:0] in_1,
  input  KbdAvaliable,
  output [31:0] Output
);

  wire [31:0] bit_extender_1_out, bit_extender_2_out, multiplexer_1_out;

  assign bit_extender_1_out = {{25{1'b0}}, in_1};  // Bit_Extender bit_extender_1
  assign bit_extender_2_out = {{25{1'b1}}, in_1};  // Bit_Extender bit_extender_2
  Multiplexer #(.width(32)) multiplexer_1 (
    .in0(bit_extender_1_out), .in1(bit_extender_2_out), .out(multiplexer_1_out), .sel(in_1[6]));  // open: en
  // Probe on {32{1'b1}}
  Multiplexer #(.width(32)) multiplexer_2 (
    .in0({32{1'b1}}), .in1(multiplexer_1_out), .out(Output), .sel(KbdAvaliable));  // open: en
endmodule
